# Fritzing sketch JAM321 (saved by Fritzing 0.7.11b)
breadboards: 1

parts:
  J1 = Basic Servo
  J2 = Infrared Proximity Sensor
  U1 = Arduino Mega

nets:
  GND: J1.gnd, J2.GND, U1.GND
  VCC: J1.vcc, J2.Vcc, U1.+5V
  N1: J1.pulse, U1.D12
  N2: J2.Vout, U1.A0

notes:
  Arduino Mega ADK
  USB A
